# Fritzing sketch Dual-Vision-Grove-Shield Rev B. (saved by Fritzing 1.0.6)
circuit board: 5.5cm x 3.55cm
breadboards: 1

parts:
  J3 = female pin header, 16 pins [form="♀ (female)"]
  J21 = female pin header, 7 pins [form="♀ (female)"]
  J23 = male pin header, 4 pins [form="♂ (male)"]
  J24 = male pin header, 4 pins [form="♂ (male)"]
  J25 = male pin header, 4 pins [form="♂ (male)"]
  J26 = male pin header, 4 pins [form="♂ (male)"]
  J27 = male pin header, 4 pins [form="♂ (male)"]
  J28 = male pin header, 4 pins [form="♂ (male)"]
  J29 = male pin header, 4 pins [form="♂ (male)"]
  J1 = female pin header, 16 pins [form="♀ (female)"]
  R1 = Resistor [tolerance=±5% power=0.25W resistance=4.7k package=THT]
  R2 = Resistor [tolerance=±5% power=0.25W resistance=4.7k package=THT]
  J22 = male pin header, 4 pins [form="♂ (male)"]
  J20 = female pin header, 7 pins [form="♀ (female)"]

nets:
  N1: J3.pin5, J27.pin1
  N2: J3.pin6, J27.pin2
  N3: J3.pin15, J21.pin6, J23.pin4, J24.pin4, J25.pin4, J26.pin4, J27.pin4, J28.pin4, J29.pin4, J1.pin2, R1.Pin_1, R2.Pin_1, J22.pin4
  N4: J21.pin5, J23.pin3, J24.pin3, J25.pin3, J26.pin3, J27.pin3, J28.pin3, J29.pin3, J1.pin1, J22.pin3
  N5: J23.pin1, J1.pin7
  N6: J23.pin2, J24.pin1, J1.pin8
  N7: J24.pin2, J25.pin1, J1.pin9
  N8: J25.pin2, J1.pin10
  N9: J26.pin1, J1.pin11
  N10: J26.pin2, J1.pin12
  N11: J28.pin1, J1.pin13
  N12: J28.pin2, J1.pin14
  N13: J29.pin1, J1.pin4, R1.Pin_0, J22.pin1, J20.pin2
  N14: J29.pin2, J1.pin3, R2.Pin_0, J22.pin2, J20.pin3

notes:
  GND
  SCL
  SDA
  3V3
  EXT-VISION-I2C
  D0
  D1
  D2
  D3
  D4
  D5
  A
  B
  D6
  D7
  TX
  RX
  VISION AI
  A2
  A1
  B2
  B1
  Rev B.
  -----
